# Fritzing sketch BasculaDigital (saved by Fritzing 0.9.5d)
circuit board: 8.57788cm x 5.85574cm
breadboards: 1

parts:
  Componente1 = HX711 Weighing Sensor Module
  Componente2 = SparkFun ESP8266 Thing
  Load_Cell1 = Load Cell - Red/white/black/green  # not connected
  U3 = LCD-16X2 [package=lcd-16x2_noholes]  # not connected
  Componente3 = Adafruit AMG8833 IR Camera FeatherWing [part_number=3622]

nets:
  VCC: Componente1.VCC, Componente2.VCC
  GND: Componente1.GND, Componente2.GND
  N1: Componente1.DO/RX, Componente2.GPIO5
  N2: Componente1.CK/TX, Componente2.GPIO2
  N3: Componente3.RX, Componente3.MISO, Componente3.SCK, Componente3.A5, Componente3.MOSI
  N4: Componente3.A1, Componente3.GND, Componente3.AREF, Componente3.A0, Componente3.A2
  N5: Componente3.USB, Componente3.EN, Componente3.VBAT
  N6: Componente3.D11, Componente3.D10, Componente3.D9, Componente3.D5, Componente3.D6

custom parts:
  Load Cell - Red/white/black/green: A rectangle load cell/weighting pressure Sensor with four wires - Red, white, black, green. Normally corresponding with E+, E-, A+, A- respectively.
  Adafruit AMG8833 IR Camera FeatherWing: Thanks to the Panasonic AMG8833 8x8 GridEYE sensor, the Thermal Camera FeatherWing adds heat-vision to any Feather main board. Using our Feather Stacking Headers or Feather Female Headers you can connect a FeatherWing on top of your Feather board and let the board take flight! This sensor from Panasonic is an 8x8 array of IR thermal sensors. When connected to your Feather it will return an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
